# Fritzing sketch wemos versoin (saved by Fritzing 0.9.9b)
breadboards: 1

parts:
  Part1 = Arduino Uno (Rev3)
  RHT1 = Humidity and Temperature Sensor RHT03
  S1 = Pushbutton [package="[THT]"]
  R1 = Resistor [tolerance=±5% resistance=220 package="0603 [SMD]"]
  J1 = Dagu DGServo 9g header (male) [package=THT]
  R2 = PHOTOCELL [package=photocell-kit]
  R3 = Resistor [tolerance=±5% power=0.25 resistance=10k package=THT]

nets:
  N1: Part1.A0, R2.P$2, R3.Pin_0
  N2: Part1.D4, R1.Pin_1
  N3: Part1.D5_PWM, RHT1.Data-signal
  N4: Part1.D6_PWM, J1.pulse
  N5: Part1.3V3, R2.P$1
  VCC: Part1.5V, RHT1.Vcc, J1.Vcc
  GND: Part1.GND, RHT1.GND_1, S1.Pin_3, S1.Pin_4, J1.gnd, R3.Pin_1
  N6: S1.Pin_2, R1.Pin_0
